// Digital circuit angstrom-cpu.dig as structural Verilog
module angstrom_cpu (
  input  CLK,
  input  in_3,
  input  in_4,
  input  in_5,
  input  in_7,
  output [11:0] out_2,
  output out_6
);

  wire decoder_1_out_0, decoder_1_out_1, decoder_1_out_2, decoder_1_out_3, decoder_1_out_4, decoder_1_out_5,
       decoder_1_out_6, decoder_1_out_7, decoder_1_out_8, decoder_1_out_9, decoder_1_out_10,
       decoder_1_out_11, decoder_1_out_12, decoder_1_out_13, decoder_1_out_14, decoder_1_out_15;
  wire [11:0] PC_out;
  wire [15:0] PGM_d;
  wire [15:12] IR_q;

  LED led_1 (.in(decoder_1_out_15));
  LED led_2 (.in(decoder_1_out_14));
  Counter #(.Bits(12), .isProgramCounter("true")) PC (.en(in_5), .C(CLK), .clr(in_3), .out(PC_out), .ovf(out_6));
  LED led_3 (.in(decoder_1_out_13));
  LED led_4 (.in(decoder_1_out_12));
  LED led_5 (.in(decoder_1_out_11));
  LED led_6 (.in(decoder_1_out_10));
  LED led_7 (.in(decoder_1_out_9));
  LED led_8 (.in(decoder_1_out_8));
  LED led_9 (.in(decoder_1_out_7));
  LED led_10 (.in(decoder_1_out_6));
  // Probe on PC_out
  ROM #(.AddrBits(12), .Bits(16), .isProgramMemory("true")) PGM (.A(PC_out), .sel(in_4), .D(PGM_d));
  LED led_11 (.in(decoder_1_out_5));
  LED led_12 (.in(decoder_1_out_4));
  LED led_13 (.in(decoder_1_out_3));
  LED led_14 (.in(decoder_1_out_2));
  Decoder #(.Selector_Bits(4)) decoder_1 (
    .sel(IR_q), .out_0(decoder_1_out_0), .out_1(decoder_1_out_1), .out_2(decoder_1_out_2),
    .out_3(decoder_1_out_3), .out_4(decoder_1_out_4), .out_5(decoder_1_out_5), .out_6(decoder_1_out_6),
    .out_7(decoder_1_out_7), .out_8(decoder_1_out_8), .out_9(decoder_1_out_9), .out_10(decoder_1_out_10),
    .out_11(decoder_1_out_11), .out_12(decoder_1_out_12), .out_13(decoder_1_out_13),
    .out_14(decoder_1_out_14), .out_15(decoder_1_out_15));
  LED led_15 (.in(decoder_1_out_1));
  LED led_16 (.in(decoder_1_out_0));
  Register #(.Bits(16)) IR (.D(PGM_d), .C(CLK), .en(in_7), .Q({IR_q, out_2}));

  // Notes on the sheet:
  //   in_4: default 1
  //   in_5: default 1
  //   in_7: default 1
  //   Opcode
  //   Instruction Decoder
  //   Args
endmodule
